# Fritzing sketch IOT (saved by Fritzing 0.9.10b)
breadboards: 1

parts:
  Mod1 = Amica NodeMCU DEVKIT 1.0
  T1 = LM35 Temperature Sensor [package="TO92 [THT]"]
  M1 = MakerFocus MAX30102

nets:
  N1: Mod1.pin1, Mod1.pin_10, Mod1.pin_26, T1.+Vs, M1.VIN
  GND: Mod1.pin2, Mod1.pin_9, Mod1.pin_25, Mod1.pin_29, T1.GND, M1.GND
  N2: Mod1.pin_13, M1.SDA
  N3: Mod1.pin_14, M1.SCL
  N4: Mod1.pin_16, T1.Vout

custom parts:
  MakerFocus MAX30102: Oximeter module using the MAX30102 chip. As usual, if you want the mounting holes in pcb, you need to drag a hole over the pad in silkscreen to actually drill the hole (by default they are not drilled)
